# Fritzing sketch rtc (saved by Fritzing 0.9.3b)
circuit board: 9.30028cm x 5.41818cm
breadboards: 1

parts:
  ZS-042_RTC1 = ZS-042 RTC Module
  Composant1 = Arduino Uno (Rev3)

nets:
  GND: ZS-042_RTC1.GND, Composant1.GND
  VCC: ZS-042_RTC1.VCC, Composant1.5V
  N1: ZS-042_RTC1.SDA, ZS-042_RTC1.SCL, Composant1.A4/SDA, Composant1.A5/SCL
