# Fritzing sketch rtc_set (saved by Fritzing 0.9.3b)
circuit board: 9.30028cm x 5.41818cm
breadboards: 1

parts:
  ZS-042_RTC1 = ZS-042 RTC Module
  Composant2 = Arduino Nano (Rev3.0)
  J1 = shrouded pin header, 6 pins [form="♂ (shrouded male)"]  # not connected
  J2 = female pin header, 6 pins [form="♀ (female)"]  # not connected

nets:
  GND: ZS-042_RTC1.GND, Composant2.GND
  VCC: ZS-042_RTC1.VCC, Composant2.5V
  N1: ZS-042_RTC1.SDA, Composant2.A4
  N2: ZS-042_RTC1.SCL, Composant2.A5
